# Fritzing sketch Schaltplan (saved by Fritzing 0.9.3b)
breadboards: 1

parts:
  M1 = DOIT Esp32 DevKit v1 (30 pins long, 11 pins width) [part_number=ESP32S-PIN30]
  M2 = DC Motor
  M4 = DC Motor
  M5 = DC Motor
  U4 = LIPO-1000mAh [package=lipo-1000]  # not connected
  S1 = H-Bridge with L298N
  S2 = H-Bridge with L298N
  M6 = DC Motor
  GY1 = MPU-6050 Board GY-521 [form="♀ (female)" package=THT]  # not connected
  Bauteil1 = Adafruit USB LiIon/LiPoly Charger [part_number="Adafruit #259"]  # not connected

nets:
  VIN: M1.VIN, S2.5V
  N1: M2.pin_1, S2.M1-01
  N2: M2.pin_2, S2.M1-02
  N3: M4.pin_1, S1.M1-01
  N4: M4.pin_2, S1.M1-02
  N5: M5.pin_1, S2.M2-01
  N6: M5.pin_2, S2.M2-02
  N7: S1.M2-01, M6.pin_2
  N8: S1.M2-02, M6.pin_1

custom parts:
  DOIT Esp32 DevKit v1 (30 pins long, 11 pins width): The DOIT Esp32 DevKit v1 is one of the development board created by DOIT to evaluate the ESP-WROOM-32 module. It is based on the ESP32 microcontroller that boasts Wifi, Bluetooth, Ethernet and Low Power support all in a single chip. (vanepp) made breadboard work, adjusted pin numbering and labels and reduced size of schematic and cleaned up pcb. This chip is 30pins long (2 x15) and 11 pins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
  H-Bridge with L298N: h-bridge
  MPU-6050 Board GY-521: Acelerometro y Giroscopio MPU-6050 Board GY-521
  Adafruit USB LiIon/LiPoly Charger: This is a Lithium Ion and Lithium Polymer battery charger based on the MCP73833. It uses a USB mini-B for connection to any computer or 'USB wall adapter'. Charging is performed in three stages: first a preconditioning charge, then a constant-current fast charge and finally a constant-voltage trickle charge to keep the battery topped-up. The fast-charge current is 500mA by default, but is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
